# Fritzing sketch LoRaSender (saved by Fritzing 0.9.10b)

parts:
  ESP8266-12F = ESP8266-12 [part_number=ESP8266-12]
  VCC1 = Battery
  DHT11 = Humidity and Temperature Sensor RHT03
  LoRa_Module = Ra-01 - LoRa Module SX1278 [part_number=SX1276]

nets:
  N1: ESP8266-12F.REST, ESP8266-12F.GPIO16
  VCC: ESP8266-12F.CH_PD, ESP8266-12F.VCC, VCC1.+, DHT11.Vcc, LoRa_Module.3.3V
  N2: ESP8266-12F.GPIO14, LoRa_Module.SCK
  N3: ESP8266-12F.GPIO12, LoRa_Module.MISO
  N4: ESP8266-12F.GPIO13, LoRa_Module.MOSI
  N5: ESP8266-12F.GPIO4, DHT11.Data-signal
  N6: ESP8266-12F.GPIO5, LoRa_Module.DIO0
  N7: ESP8266-12F.GPIO2, LoRa_Module.RESET
  N8: ESP8266-12F.GPIO15, LoRa_Module.NSS
  GND: ESP8266-12F.GND, VCC1.-, DHT11.GND_2, LoRa_Module.GND

notes:
  ESP8266-12F
  SX1276
  D3 (GPIO2)
  REST
  D1 (GPIO5)
  DI00
  D5 (GPIO14)
  SCK
  D6 (GPIO12)
  MISO
  D7 (GPIO13)
  MOSI
  D8 (GPIO15)
  NSS
  GND
  GND
  3V3
  VCC
  ESP8266-12F
  DHT11
  D2 (GPIO4)
  Data
  GND
  GND
  3V3
  3V3

custom parts:
  Ra-01 - LoRa Module SX1278: The Ra-01 LoRa Module featuring the SX1278 engine by Semtech. Module by AI-Thinker. Module (Ra-01) specifications from: https://www.banggood.com/Ra-01-Smart-Electronics-SX1278-LoRa-Spread-Spectrum-Wireless-Module-Ultra-Far-10KM-433M-p-1130769.html Description: Power supply: DC1.8-3.7V(3.3V) Chip: SX1278 Frequency: 433Mhz Operating temperature: -40~+85°C On Sheild Description (may vary by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
